# Fritzing sketch hammond_headphone_lineout (saved by Fritzing 0.9.10b)
breadboards: 1

parts:
  Speaker_on/off_switch = Taiway 100-SP-X-T1 SPDT Miniature Toggle Switch [part_number=100-SP-X-T1-0-0-B1-M2 package=THT]
  JP1 = Header 3 [package=jst-3-smd]
  Hammond_Speaker_voice_coil = SPEAKER [package=pcb_mount_speaker]
  Hammond_Amp_Speaker_out = mystery part, 2 pins [chip_label=?]
  R1 = Resistor [tolerance=±20% resistance=10 power=10W package="0603 [SMD]"]
  R2 = Resistor [tolerance=±5% power=0.25 resistance=1k package=THT]
  Non-polarized = Capacitor Polarized [mn=15uF package=panasonic_h13]
  Line_Out_1/4" = 3.5mm Audio Jack [package=audio-jack-3.5mm-smd]
  Headphone_Volume = Rotary Potentiometer (Large) [maximum_resistance=10kΩ knob_status=50% power=0.5W package=THT]
  Line_Out_Volume = Rotary Potentiometer (Large) [maximum_resistance=10kΩ knob_status=50% power=0.5W package=THT]
  R5 = Resistor [tolerance=±5% power=0.25 resistance=22 package=THT]
  R3 = Resistor [tolerance=±5% power=0.25 resistance=22 package=THT]
  Headphone_1/4" = 3.5mm Audio Jack [package=audio-jack-3.5mm-smd]
  Headphone_2_5mm = 2.5mm Audio Jack [package=stereojack2.5mm_specia_pogopins]
  R4 = Resistor [tolerance=±5% power=0.25 resistance=22 package=THT]

nets:
  N1: Speaker_on/off_switch.COM, JP1.1, Hammond_Amp_Speaker_out.pin1
  N2: Speaker_on/off_switch.L1, R1.Pin_0, R2.Pin_0, R3.Pin_0
  N3: Speaker_on/off_switch.L2, JP1.2, Hammond_Speaker_voice_coil.+
  N4: JP1.3, Hammond_Speaker_voice_coil.-, Hammond_Amp_Speaker_out.pin2, R1.Pin_1, Headphone_Volume.leg2, Line_Out_Volume.leg2
  N5: R2.Pin_1, Line_Out_Volume.leg1
  N6: Non-polarized.+, Line_Out_1/4".RIGHT
  N7: Non-polarized.-, Line_Out_Volume.wiper
  N8: Headphone_Volume.leg1, R3.Pin_1
  N9: Headphone_Volume.wiper, R5.Pin_0, R4.Pin_0
  N10: R5.Pin_1, Headphone_1/4".RIGHT, Headphone_2_5mm.RIGHT
  N11: Headphone_1/4".LEFT, Headphone_2_5mm.LEFT, R4.Pin_1
